// Logisim project aci.circ as structural Verilog: 1 circuit, main circuit main
module main (
);

  wire clock_1_out, d_ff_1_q, d_ff_1_qn, nand_1_out, nor_1_out, nor_2_out, nor_3_out;

  Clock clock_1 (.out(clock_1_out));
  nor nor_1 (nor_1_out, 1'b0, 1'b0);
  nor nor_2 (nor_2_out, 1'b0, 1'b0);
  nand nand_1 (nand_1_out, nor_1_out, nor_2_out, clock_1_out);
  LED led_1 (.in(nand_1_out));
  nor nor_3 (nor_3_out, nand_1_out, 1'b0);
  D_Flip_Flop d_ff_1 (.clk(nor_3_out), .D(d_ff_1_qn), .Q(d_ff_1_q), .Qn(d_ff_1_qn));  // open: preset, en, reset
  LED led_2 (.in(d_ff_1_q));

  // Notes on the sheet:
  //   4KCS
  //   A11
  //   A10
  //   A9
  //   CLK2
  //   A8
endmodule
